# Fritzing sketch wiring (saved by Fritzing 1.0.4)
breadboards: 1

parts:
  M1 = DOIT Esp32 DevKit v1 (30 pins long, 11 pins width) [part_number=ESP32S-PIN30]
  MPU6050 = InvenSense MPU6050
  LED1 = LED - 3mm [color="Red (633nm)" current=0.030A package="3 mm [THT]"]
  R1 = Resistor [tolerance=±5% resistance=220 package="1206 [SMD]"]

nets:
  3V3: M1.3V3, MPU6050.VCC
  GND: M1.GND, MPU6050.GND, LED1.cathode
  N1: M1.D18, MPU6050.SCL
  N2: M1.D19, MPU6050.SDA
  N3: M1.D26, R1.Pin_1
  N4: LED1.anode, R1.Pin_0

custom parts:
  DOIT Esp32 DevKit v1 (30 pins long, 11 pins width): The DOIT Esp32 DevKit v1 is one of the development board created by DOIT to evaluate the ESP-WROOM-32 module. It is based on the ESP32 microcontroller that boasts Wifi, Bluetooth, Ethernet and Low Power support all in a single chip. (vanepp) made breadboard work, adjusted pin numbering and labels and reduced size of schematic and cleaned up pcb. This chip is 30pins long (2 x15) and 11 pins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
